# Fritzing sketch Untitled Sketch (saved by Fritzing 0.9.3b)
breadboards: 1

parts:
  Rc = Resistor [tolerance=±5% resistance=2.2k package=THT]
  Rc_2 = Resistor [tolerance=±5% resistance=2.2k package=THT]
  R2 = Resistor [tolerance=±5% resistance=6.8k package=THT]
  R2_2 = Resistor [tolerance=±5% resistance=6.8k package=THT]
  Re = Resistor [tolerance=±5% resistance=470 package=THT]
  R1 = Resistor [tolerance=±5% resistance=15k package=THT]
  R1_2 = Resistor [tolerance=±5% resistance=15k package=THT]
  Q1 = NPN-Transistor [package="TO92 [THT]"]
  Q2 = NPN-Transistor [package="TO92 [THT]"]
  パーツ1 = Arduino Leonardo (Rev3b)
  D1 = Rectifier Diode [part_number=1N4001 package="300 mil [THT]"]
  D2 = Rectifier Diode [part_number=1N4001 package="300 mil [THT]"]
  R3 = Resistor [tolerance=±5% resistance=1k package=THT]
  R3_2 = Resistor [tolerance=±5% resistance=1k package=THT]
  R3_3 = Resistor [tolerance=±5% resistance=1k package=THT]
  R3_4 = Resistor [tolerance=±5% resistance=1k package=THT]

nets:
  12V: Rc.Pin_0, Rc_2.Pin_0
  N1: Rc.Pin_1, R1.Pin_0, Q1.C, D1.anode
  N2: Rc_2.Pin_1, R1_2.Pin_1, Q2.C, D2.anode
  N3: R2.Pin_0, R1_2.Pin_0, Q1.B
  GND: R2.Pin_1, R2_2.Pin_1, Re.Pin_1, パーツ1.GND, R3_3.Pin_1, R3_4.Pin_1
  N4: R2_2.Pin_0, R1.Pin_1, Q2.B
  N5: Re.Pin_0, Q1.E, Q2.E
  N6: パーツ1.A0, R3.Pin_1
  N7: パーツ1.A1, R3_2.Pin_1
  N8: D1.cathode, R3_2.Pin_0, R3_4.Pin_0
  N9: D2.cathode, R3.Pin_0, R3_3.Pin_0
