# Fritzing sketch 入出力測定回路 (saved by Fritzing 0.9.3b)
breadboards: 1

parts:
  U1 = 74HC00 [part_number=SN74HC00N package="DIP14 [THT]"]
  C1 = Ceramic Capacitor [capacitance=100nF package="100 mil [THT, multilayer]"]

nets:
  N1: U1.1B, U1.GND, U1.3A, U1.3B, U1.4A, U1.4B
  N2: U1.1Y, U1.2A, U1.2B
  N3: U1.VCC, C1.0, C1.1

custom parts:
  74HC00: Quad 2 input NAND logic gates.
