# Fritzing sketch 波形整形回路の静特性測定回路 (saved by Fritzing 0.9.3b)
breadboards: 1

parts:
  U1 = 74HC00 [part_number=SN74HC00N package="DIP14 [THT]"]
  C1 = Ceramic Capacitor [capacitance=100nF package="100 mil [THT, multilayer]"]
  D1 = Rectifier Diode [part_number=1N4001 package="300 mil [THT]"]
  R1 = Resistor [tolerance=±5% resistance=220 package=THT]  # not connected

nets:
  N1: U1.1A, D1.cathode
  N2: U1.1B, D1.anode
  N3: U1.1Y, U1.2A, U1.2B
  N4: U1.GND, U1.3A, U1.3B, U1.4A, U1.4B, C1.0
  N5: U1.VCC, C1.1

custom parts:
  74HC00: Quad 2 input NAND logic gates.
