# Fritzing sketch Untitled Sketch (saved by Fritzing 0.9.3b)
breadboards: 1

parts:
  U1 = 74HC00 [part_number=SN74HC00N package="DIP14 [THT]"]
  U2 = 74HC00 [part_number=SN74HC00N package="DIP14 [THT]"]
  U3 = 74HC00 [part_number=SN74HC00N package="DIP14 [THT]"]
  R1 = Trimmer Potentiometer [maximum_resistance=10kΩ package=THT]  # not connected
  C1 = Ceramic Capacitor [capacitance=100nF package="100 mil [THT, multilayer]"]
  C2 = Ceramic Capacitor [capacitance=100nF package="100 mil [THT, multilayer]"]
  C3 = Ceramic Capacitor [capacitance=100nF package="100 mil [THT, multilayer]"]
  D1 = Rectifier Diode [part_number=1N4001 package="300 mil [THT]"]
  R2 = Resistor [tolerance=±5% resistance=220 package=THT]
  C4 = Ceramic Capacitor [capacitance=100nF package="100 mil [THT, multilayer]"]
  R3 = Resistor [tolerance=±5% resistance=4.7k package=THT]

nets:
  N1: U1.1B, D1.cathode, R2.Pin_0
  N2: U1.1Y, U1.2A, U1.2B
  N3: U1.2Y, R2.Pin_1, C4.0
  GND: U1.GND, U1.4A, U1.4B, U2.GND, U2.3Y, U2.3A, U3.GND, U3.3A, U3.3B, R3.Pin_1
  N4: U1.3A, C4.1
  N5: U1.3B, R3.Pin_0
  VCC: U1.VCC, U2.VCC, U3.VCC, C1.0, C1.1, C2.0, C2.1, C3.0, C3.1

custom parts:
  74HC00: Quad 2 input NAND logic gates.
